# Fritzing sketch mainpart-skema (saved by Fritzing 0.8.7b)

parts:
  U1 = ESP 32 DEVKIT DOIT
  Part1 = Adafruit RFM9x LoRa Radio [part_number="Adafruit #3072 and #3073"]
  ANT1 = Antenna
  Sensor1 = Gas Sensor Breakout Board
  Part2 = LCD1602-I2C
  Part3 = Voltage Sensor 25V
  TP1 = TP4056 [chip_label=TP4056 package="DIP (Dual Inline) [THT]"]
  Bat1 = battery_holder_dual_18650 [part_number=TBH-18650-2A-P]
  S1 = Square Pushbutton

nets:
  N1: U1.D23, Part1.MOSI
  N2: U1.D22, U1.D18, U1.D5, Part1.SCK, Part1.CS, Part2.SCL
  N3: U1.D21, Part2.SDA
  N4: U1.D19, Part1.MISO
  VIN: U1.Vin, Part1.VIN, Sensor1.5V, Part2.VCC, S1.leg0
  GND: U1.GND, Part1.GND, Sensor1.GND, Part2.GND, Part3.-, TP1.pin6
  N5: U1.D14, Part1.RST
  N6: U1.D26, Part1.DIO0
  N7: U1.D35, Part3.S
  N8: U1.D34, Sensor1.AOUT
  N9: Part1.ANTENNA, ANT1.antenna_lead
  N10: Part3.GND, TP1.pin5, Bat1.+#0, Bat1.+#1
  N11: Part3.VCC, Part3.+, TP1.pin4, Bat1.+#2, Bat1.+#3
  N12: TP1.pin3, S1.leg1

custom parts:
  Adafruit RFM9x LoRa Radio: Sending data over long distances is like magic, and now you can be a magician with this range of powerful and easy-to-use radio modules. Sure, sometimes you want to talk to a computer (a good time to use WiFi) or perhaps communicate with a Phone (choose Bluetooth Low Energy!) but what if you want to send data very far? Most WiFi, Bluetooth, Zigbee and other wireless chipsets use 2.4GHz, which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
  Gas Sensor Breakout Board: Gas sensor breakout board. Input voltage is 5V. Sensor output is available in analog and digital.
  LCD1602-I2C: A standard character display, usually with 2x16 characters. Comes in many colors with LCM1602 IIC attached.
  TP4056: A DIP stand-in part for whatever IC you want. With 6 pins on a 300mil dual inline package (DIP) footprint.
  battery_holder_dual_18650: TBH-18650-2A-P dual 18650 battery holder.
