# Fritzing sketch monitoring-air-sungai (saved by Fritzing 0.9.3b)

parts:
  U1 = ESP 32 DEVKIT DOIT
  Part1 = LCD1602-I2C

nets:
  N1: U1.D22, U1.D18, Part1.SCL
  N2: U1.D21, Part1.SDA
  VIN: U1.Vin, Part1.VCC
  GND: U1.GND, Part1.GND

custom parts:
  LCD1602-I2C: A standard character display, usually with 2x16 characters. Comes in many colors with LCM1602 IIC attached.
