# Fritzing sketch mqtt-smart-home-skema (saved by Fritzing 0.8.7b)

parts:
  U1 = ESP 32 DEVKIT DOIT
  U2 = 2-Channel 5v Relay Shield [package=relay-2ch5v10a]
  Mod1 = generic-ac-power-supply [package=THT]
  J1 = 220v plug
  BULB1 = Incandescent light bulb small [package="bulb sm"]
  J2 = 120V duplex outlet_1

nets:
  N1: U1.D22, U1.TX2, U1.RX2, U2.IN1, U2.IN2
  VIN: U1.Vin, U2.VCC, Mod1.pin3#2
  GND: U1.GND, U2.GND, Mod1.pin3#3
  N2: U2.K1-In, U2.K2-In, Mod1.pin1, J1.pin1
  N3: U2.K1-On, J2.N2, J2.N1
  N4: U2.K2-On, BULB1.2
  N5: Mod1.pin2, J1.pin2, BULB1.1, J2.H1, J2.H2

custom parts:
  2-Channel 5v Relay Shield: 2 Channel 5v Relay Shield w. 2x SPD-06VDC-SD-C
  generic-ac-power-supply: Generic ac power supply module. Use as is, or customize the svgs to fit your particular device (as they are all different.) Provides AC input and single DC output. PCB is generic and will need modifications if you intend to do a pcb mount.
  220v plug: Generic 220V AC plug.
  120V duplex outlet_1: 120V duplex outlet.
