# Fritzing sketch skema-lengan-robot-pemetik-cabe (saved by Fritzing 0.8.7b)

parts:
  Part1 = Adafruit PCA9685 PWM/Servo Breakout [part_number=815]
  U1 = ESP 32 DEVKIT DOIT
  J1 = Basic Servo
  J2 = Basic Servo
  J3 = Basic Servo
  J4 = Basic Servo
  J5 = 220v plug
  Mod1 = generic-ac-power-supply [package=THT]

nets:
  N1: Part1.PWM3, J3.pulse
  VCC: Part1.5.0V, Part1.VCC, U1.Vin, J1.vcc, J2.vcc, J3.vcc, J4.vcc, Mod1.pin3#2
  GND: Part1.GND, U1.GND, J1.gnd, J2.gnd, J3.gnd, J4.gnd, Mod1.pin3#3
  N2: Part1.PWM2, J4.pulse
  N3: Part1.PWM1, J1.pulse
  N4: Part1.PWM0, J2.pulse
  N5: Part1.SDA, U1.D21
  N6: Part1.SCL, U1.D22, U1.D18
  N7: J5.pin1, Mod1.pin1
  N8: J5.pin2, Mod1.pin2

notes:
  Servo 1 @Pin_0 (Bawah-Atas)
  Servo 2 @Pin_1 (Kiri-Kanan)
  Servo 3 @Pin_2 (Mundur-Maju)
  Servo 4 @Pin_3 (Lepas-Jepit)

custom parts:
  Adafruit PCA9685 PWM/Servo Breakout: Using only two pins, control 16 free-running PWM outputs! I2C-controlled PWM driver with a built in clock. Unlike the TLC5940 family, you do not need to continuously send it signal tying up your microcontroller, its completely free running! 5V compliant, which means you can control it from a 3.3V microcontroller and still safely drive up to 6V outputs (this is good for when you want to control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
  220v plug: Generic 220V AC plug.
  generic-ac-power-supply: Generic ac power supply module. Use as is, or customize the svgs to fit your particular device (as they are all different.) Provides AC input and single DC output. PCB is generic and will need modifications if you intend to do a pcb mount.
