# Fritzing sketch skema_portal_parkir (saved by Fritzing 0.9.2b)
breadboards: 2

parts:
  U1 = ESP 32 DEVKIT DOIT
  M1 = fc-51 [package=THT]
  M2 = fc-51 [package=THT]
  Mod1 = KY-018 Photoresistor Module [package="Breakout board"]
  M3 = ac light dimmer-4terminal
  J1 = Basic Servo
  M4 = ac light dimmer-4terminal
  Part1 = SRF05 Ultrasonic Rangefinder
  Part2 = SRF05 Ultrasonic Rangefinder
  J2 = 220v plug
  BULB1 = Incandescent light bulb small [package="bulb sm"]
  BULB2 = Incandescent light bulb small [package="bulb sm"]
  M5 = WX-DC12003 [package=THT]
  J3 = 220v plug

nets:
  VCC: U1.Vin, J1.vcc, Part1.VCC, Part2.VCC, M5.DC_OUT+
  GND: U1.GND, J1.gnd, Part1.GND, Part2.GND, M5.DC_OUT-
  N1: U1.D13, U1.D14, M3.Z-C
  N2: U1.D12, M3.PWM
  N3: U1.D26, Part1.Echo
  N4: U1.D25, Part1.Trig
  N5: U1.D33, Part2.Echo
  N6: U1.D32, Part2.Trig
  N7: M1.pin2, M2.pin2, Mod1.-, M3.GND
  VIN: M1.pin3, M2.pin3, Mod1.Vin, M3.VCC
  N8: M3.LOAD1, BULB2.2
  N9: M3.LOAD2, BULB2.1
  N10: M3.AC-IN1, J2.pin1
  N11: M3.AC-IN2, J2.pin2
  N12: M4.LOAD1, BULB1.2
  N13: M4.LOAD2, BULB1.1
  N14: M5.IN-L, J3.pin2
  N15: M5.IN-N, J3.pin1

custom parts:
  KY-018 Photoresistor Module: KY-018 Photoresistor module, used to measure light intensity. It can determine the presence or absence of light.
  ac light dimmer-4terminal: ac light dimmer module 4terminal.
  220v plug: Generic 220V AC plug.
  WX-DC12003: Ac to DC power supply 110/220V in 5v 700ma or 12 V 300ma out.
