# Fritzing sketch smart-door-lock-skema (saved by Fritzing 0.8.7b)

parts:
  ESP32_-_Back1 = ESP32 - CAM
  A1 = PIR sensor
  M1 = DC Motor
  KY-1 = Keyes Relay [package=THT]
  Mod1 = generic-ac-power-supply [package=THT]
  J1 = 220v plug
  U1 = LM2596 step down module

nets:
  N1: ESP32_-_Back1.GPIO13, A1.SIG
  N2: ESP32_-_Back1.GPIO12, KY-1.signal
  N3: ESP32_-_Back1.GND#7, M1.pin_1, Mod1.pin3#3, U1.IN-, U1.OUT-
  N4: ESP32_-_Back1.5V, U1.OUT+
  3.3V: ESP32_-_Back1.3.3V, A1.VDD, KY-1.power
  N5: ESP32_-_Back1.GND#12, A1.GND, KY-1.ground
  N6: M1.pin_2, KY-1.NO
  N7: KY-1.C, Mod1.pin3#2, U1.IN+
  N8: Mod1.pin1, J1.pin1
  N9: Mod1.pin2, J1.pin2

notes:
  Solenoid Door Lock
  Adaptor AC-DC 12V

custom parts:
  ESP32 - CAM: The ESP32-CAM has a very competitive small-size camera module that can operate independently as a minimum system with a footprint of only 27*40.5*4.5mm and a deep sleep current of up to 6mA.
  PIR sensor: Generic PIR sensor
  Keyes Relay: The Keyes 5V relay module is suitable for SCM development, home appliance control. It uses a 5V~12V TIL control signal which can control DC / AC signal.
  generic-ac-power-supply: Generic ac power supply module. Use as is, or customize the svgs to fit your particular device (as they are all different.) Provides AC input and single DC output. PCB is generic and will need modifications if you intend to do a pcb mount.
  220v plug: Generic 220V AC plug.
  LM2596 step down module: LM2596 DC-DC step down power supply module 3 A.
