# Fritzing sketch skema-smoke-flame-detector-220723 (saved by Fritzing 0.9.2b)

parts:
  U1 = ESP 32 DEVKIT DOIT
  Part1 = MQ-7 breakout
  U2 = 2-Channel 5v Relay Shield [package=relay-2ch5v10a]
  J1 = Piezo Speaker  # not connected
  Mod1 = KY-026 Flame Sensor Module [package="Breakout board"]
  F1 = Fan - Ventilador [package=THT]
  JACK1 = 2.1mm Barrel Jack with Terminal Block
  R1 = Resistor [tolerance=±5% resistance=200 package="1206 [SMD]"]
  R2 = Resistor [tolerance=±5% resistance=100 package="1206 [SMD]"]

nets:
  N1: U1.Vin, JACK1.POS
  N2: U1.GND, JACK1.NEG
  N3: U1.D26, Mod1.D0
  N4: U1.D33, R1.Pin_1
  N5: U1.D32, U2.IN1
  N6: Part1.DO, R1.Pin_0
  N7: Part1.AO, R2.Pin_0
  N8: U2.K1-In, F1.5V

custom parts:
  MQ-7 breakout: SKU: 101282
  2-Channel 5v Relay Shield: 2 Channel 5v Relay Shield w. 2x SPD-06VDC-SD-C
  KY-026 Flame Sensor Module: KY-026 Flame Sensor Module reacts in the presence of fire.
  Fan - Ventilador: Ventilador de 2 pines, se encuentra comunmente en computadoras de escritorio
