# Fritzing sketch ph-tanah-penyiram-2-mode (saved by Fritzing 0.9.2b)

parts:
  M1 = WX-DC12003 [package=THT]
  J1 = 220v plug
  U1 = ESP 32 DEVKIT DOIT
  JP1 = Header 3 [package=screwterminal-3.5mm-3_lock.007s]
  Mod1 = KY-019 5V Relay Module [package="Breakout board"]
  JP2 = Header 3 [package=screwterminal-3.5mm-3_lock.007s]
  WATER_PUMP1 = water pump/motor
  JP3 = Header 3 [package=screwterminal-3.5mm-3_lock.007s]
  Boost_Convertor1 = Boost Convertor [part_number=XL6009E1 package=THT]
  Mod2 = KY-019 5V Relay Module [package="Breakout board"]
  VALVE1 = Plastic Solenoid Valve
  Capacitive_Soil_Moisture_Sensor1 = DFRobot Capacitive Soil Moisture Sensor V1.0 [part_number=SEN0193]  # not connected
  DS1 = DS18B20 1-Wire Temperature Sensor Probe
  R1 = Resistor [tolerance=±5% resistance=4.7k package="0805 [SMD]"]
  Part1 = LCD1602-I2C
  M2 = pt100

nets:
  N1: M1.IN-L, J1.pin2
  N2: M1.IN-N, J1.pin1
  N3: M1.DC_OUT+, U1.Vin
  N4: M1.DC_OUT-, U1.GND
  N5: U1.D22, U1.D5, U1.D4, U1.3V3, JP1.3, Part1.SCL
  N6: U1.D21, Part1.SDA
  N7: U1.D13, U1.D14, M2.pin1, M2.pin2
  N8: Mod1.S, JP2.3
  N9: Mod1.+, JP2.2
  N10: Mod1.-, JP2.1
  N11: Mod1.Common, WATER_PUMP1.pin_2
  N12: JP3.1, Boost_Convertor1.Negative_Input
  N13: JP3.2, Boost_Convertor1.Positive_Input
  N14: JP3.3, Mod2.S
  N15: Boost_Convertor1.Negative_Output, VALVE1.no_name_yet#2
  N16: Boost_Convertor1.Positive_Output, Mod2.NO
  N17: Mod2.Common, VALVE1.no_name_yet#1
  N18: DS1.DQ, R1.Pin_0

notes:
  Main System
  Output Solenoid
  Output Pump

custom parts:
  WX-DC12003: Ac to DC power supply 110/220V in 5v 700ma or 12 V 300ma out.
  220v plug: Generic 220V AC plug.
  KY-019 5V Relay Module: KY-019 5V Relay module, used to control AC circuits. (Special thanks to vanepp for fixing the PCB holes and other errors)
  water pump/motor: WATER PUMP BY ARDUBLOCKTR
  Boost Convertor: DC to DC boost convertor
  DFRobot Capacitive Soil Moisture Sensor V1.0: DFRobot Capacitive Soil Moisture Sensor V1.0 This product measures soil moisture levels by capacitive sensing, rather than resistive sensing like other types of moisture sensor. It is made of a corrosion resistant material giving it a long service life. Insert it into soil and impress your friends with the real-time soil moisture data! The product includes an on-board voltage regulator which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
  LCD1602-I2C: A standard character display, usually with 2x16 characters. Comes in many colors with LCM1602 IIC attached.
  pt100: CrocSee RTD Pt100 Temperature Sensor Probe 3 Wires 2M Cable Thermocouple -58~572°F (-50-300°C) 1/2" BSP Thread.
