# Fritzing sketch ukur-hemat-listrik (saved by Fritzing 0.8.7b)

parts:
  Part1 = Arduino Mega ADK (Rev3)
  Part2 = Current Sensor 5A
  U1 = 4-Channel 5v Relay Shield [package=relay-4ch5v10a]
  RCWL-0516_Microwave_Radar_Motion_Sensor1 = RCWL-0516 Microwave Radar Motion Sensor Module
  LCD2004-I2C1 = LCD2004-I2C
  Part3 = Current Sensor 5A
  Part4 = Current Sensor 5A
  Part5 = Current Sensor 5A
  J1 = 120V duplex outlet_1
  J2 = 120V duplex outlet_1
  J3 = 220v plug
  SD_card_module1 = SD Card Module
  PCB2 = RTC_DS1302_module

nets:
  N1: Part1.A0, Part1.A1, Part1.A2, Part1.A3, Part2.2, Part2.OUT, Part3.2, Part3.OUT, Part4.2, Part4.OUT, Part5.2, Part5.OUT, J3.pin2
  N2: Part1.D21/SCL, LCD2004-I2C1.SCL
  N3: Part1.D20/SDA, LCD2004-I2C1.SDA
  GND: Part1.GND, Part2.GND, U1.GND, RCWL-0516_Microwave_Radar_Motion_Sensor1.GND, LCD2004-I2C1.GND, Part3.GND, Part4.GND, Part5.GND, SD_card_module1.GND, PCB2.GND
  N4: Part1.D11_PWM, U1.IN4
  N5: Part1.D10_PWM, U1.IN3
  N6: Part1.D9_PWM, U1.IN2
  N7: Part1.D8_PWM, U1.IN1
  VCC: Part1.5V, Part2.VCC, U1.VCC, RCWL-0516_Microwave_Radar_Motion_Sensor1.VIN, LCD2004-I2C1.VCC, Part3.VCC, Part4.VCC, Part5.VCC, SD_card_module1.+3.3, SD_card_module1.+5, PCB2.VCC
  N8: Part1.D2_PWM, PCB2.CLK
  N9: Part1.D3_PWM, PCB2.DAT
  N10: Part1.D4_PWM, PCB2.RST
  N11: Part1.D6_PWM, RCWL-0516_Microwave_Radar_Motion_Sensor1.OUT
  N12: Part1.D50/MISO, SD_card_module1.MISO
  N13: Part1.D51/MOSI, SD_card_module1.MOSI
  N14: Part1.D52/SCK, SD_card_module1.SCK
  N15: Part1.D53/SS, SD_card_module1.CS
  N16: Part2.1, U1.K4-Off
  N17: U1.K1-Off, Part5.1
  N18: U1.K1-On, J2.N2
  N19: U1.K2-Off, Part4.1
  N20: U1.K2-On, J2.N1
  N21: U1.K3-Off, Part3.1
  N22: U1.K3-On, J1.N2
  N23: U1.K4-On, J1.N1
  N24: J1.H1, J1.H2, J2.H1, J3.pin1

custom parts:
  4-Channel 5v Relay Shield: 4 Channel 5v Relay Shield w. 2x SPD-06VDC-SD-C
  RCWL-0516 Microwave Radar Motion Sensor Module: The RCWL-0516 is a microwave radar motion sensor module. Input voltage is 4V to 28V. The 3V3 pin is a power output.
  LCD2004-I2C: A standard character display with 4x20 characters. Comes in many colors with LCM2004 IIC attached.
  120V duplex outlet_1: 120V duplex outlet.
  220v plug: Generic 220V AC plug.
  SD Card Module: SD Card Module Slot Socket Reader For Arduino ARM MCU
  RTC_DS1302_module: Arduino module DS1302 SPI Real Time Clock
