# Fritzing sketch oscilloscope (saved by Fritzing 0.9.3b)

parts:
  Part1 = Arduino Mega 2560 (Rev3)
  Part2 = Voltage Sensor 25V
  J1 = 220v plug
  Mod1 = generic-ac-power-supply [package=THT]

nets:
  N1: Part1.A0, Part2.S
  N2: Part1.GND, Part2.-, Mod1.pin3#3
  N3: Part1.VIN, Mod1.pin3#2
  N4: J1.pin1, Mod1.pin1
  N5: J1.pin2, Mod1.pin2

notes:
  +Vin
  -Vin

custom parts:
  220v plug: Generic 220V AC plug.
  generic-ac-power-supply: Generic ac power supply module. Use as is, or customize the svgs to fit your particular device (as they are all different.) Provides AC input and single DC output. PCB is generic and will need modifications if you intend to do a pcb mount.
