# Fritzing sketch signal-generator (saved by Fritzing 0.9.3b)

parts:
  Part1 = LCD1602-I2C
  Part2 = Arduino Uno (Rev3) - ICSP
  RE2 = KY-040 Rotary encoder [package=THT]
  U1 = ENCODER-QUADRATURE [package=encoder-16mm-quad]
  U2 = ENCODER-QUADRATURE [package=encoder-16mm-quad]
  Part3 = Adafruit MCP4725 [part_number="Adafruit #935"]

nets:
  GND: Part1.GND, Part2.GND, RE2.GND, U1.C, U2.C, Part3.GND
  VCC: Part1.VCC, Part2.5V, U1.A, U2.A, Part3.VCC
  N1: Part1.SDA, Part2.A4/SDA, Part3.SDA
  N2: Part1.SCL, Part2.A5/SCL, Part3.SCL
  N3: Part2.A0, U1.B
  N4: Part2.A1, U2.B
  N5: Part2.D2, RE2.CLK
  N6: Part2.D3_PWM, RE2.DT
  N7: Part2.D4, RE2.SW

notes:
  +Vout
  -Vout

custom parts:
  LCD1602-I2C: A standard character display, usually with 2x16 characters. Comes in many colors with LCM1602 IIC attached.
  KY-040 Rotary encoder: KY-040 Rotary Encoder with switch on breakout borad from AZ Delivery
  Adafruit MCP4725: Your microcontroller probably has an ADC (analog -> digital converter) but does it have a DAC (digital -> analog converter)??? Now it can! This breakout board features the easy-to-use MCP4725 12-bit DAC. Control it via I2C and send it the value you want it to output, and the VOUT pin will have it. Great for audio / analog projects, such as when you can't use PWM but need a sine wave or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
