# Fritzing sketch pelipat-pakaian (saved by Fritzing 0.9.2b)

parts:
  Part1 = Arduino Uno (Rev3) - ICSP
  Part2 = Bluetooth HC-05
  PWM1 = PCA9685 16x12-bit PWM Breakout
  J1 = Basic Servo
  J2 = Basic Servo
  J3 = Basic Servo
  M1 = WX-DC12003 [package=THT]
  J4 = 220v plug

nets:
  N1: Part1.A4/SDA, PWM1.no_name_yet#603
  N2: Part1.A5/SCL, PWM1.no_name_yet#604
  N3: Part1.D0/RX, Part2.TXD
  N4: Part1.D1/TX, Part2.RXD
  5V: Part1.5V, Part2.VCC, PWM1.no_name_yet#605
  GND: Part1.GND, Part2.GND, PWM1.no_name_yet#601, PWM1.no_name_yet#1000, PWM1.no_name_yet#1001, PWM1.no_name_yet#1002, J1.gnd, J2.gnd, J3.gnd, M1.DC_OUT-
  N5: PWM1.no_name_yet#0, J3.pulse
  N6: PWM1.no_name_yet#1, J1.pulse
  N7: PWM1.no_name_yet#2, J2.pulse
  VCC: PWM1.no_name_yet#100, PWM1.no_name_yet#101, PWM1.no_name_yet#102, PWM1.no_name_yet#606, J1.vcc, J2.vcc, J3.vcc, M1.DC_OUT+
  N8: M1.IN-L, J4.pin2
  N9: M1.IN-N, J4.pin1

custom parts:
  WX-DC12003: Ac to DC power supply 110/220V in 5v 700ma or 12 V 300ma out.
  220v plug: Generic 220V AC plug.
