# Fritzing sketch pengaman-ruang-rcwl (saved by Fritzing 0.9.2b)

parts:
  Part1 = Arduino Uno (Rev3) - ICSP
  ESP32_-_Back1 = ESP32 - CAM
  RCWL-0516_Microwave_Radar_Motion_Sensor1 = RCWL-0516 Microwave Radar Motion Sensor Module

nets:
  N1: Part1.D12/MISO, RCWL-0516_Microwave_Radar_Motion_Sensor1.OUT
  N2: Part1.D13/SCK, ESP32_-_Back1.GPIO12
  5V: Part1.5V, ESP32_-_Back1.5V, RCWL-0516_Microwave_Radar_Motion_Sensor1.VIN
  GND: Part1.GND, ESP32_-_Back1.GND, RCWL-0516_Microwave_Radar_Motion_Sensor1.GND

custom parts:
  ESP32 - CAM: The ESP32-CAM has a very competitive small-size camera module that can operate independently as a minimum system with a footprint of only 27*40.5*4.5mm and a deep sleep current of up to 6mA.
  RCWL-0516 Microwave Radar Motion Sensor Module: The RCWL-0516 is a microwave radar motion sensor module. Input voltage is 4V to 28V. The 3V3 pin is a power output.
