# Fritzing sketch skema-safepil (saved by Fritzing 0.9.2b)

parts:
  U1 = SWITCH_SPDT [package=kps-1290]
  WeMos_D1_Mini_Lite1 = WeMos D1 Mini Lite
  J1 = Piezo Speaker
  TP1 = TP4056 [chip_label=TP4056 package="DIP (Dual Inline) [THT]"]
  U2 = LIPO-2000mAh [package=lipo-2000]

nets:
  N1: U1.P, WeMos_D1_Mini_Lite1.5V
  N2: U1.S, TP1.pin3
  N3: WeMos_D1_Mini_Lite1.D8, J1.pin2
  N4: WeMos_D1_Mini_Lite1.G, J1.pin1, TP1.pin6
  N5: TP1.pin4, U2.+
  N6: TP1.pin5, U2.-

custom parts:
  WeMos D1 Mini Lite: A simple wifi board with 1MB flash based on ESP-8285
  TP4056: A DIP stand-in part for whatever IC you want. With 6 pins on a 300mil dual inline package (DIP) footprint.
