# Fritzing sketch tempat-sampah-opencv (saved by Fritzing 0.9.2b)
breadboards: 1

parts:
  BT1 = Bluetooth HC-06u [package=THT]
  J1 = Basic Servo
  M1 = WX-DC12003 [package=THT]
  J2 = 220v plug
  Part1 = Arduino Uno (Rev3) - ICSP
  J3 = Basic Servo

nets:
  VCC: BT1.VCC, J1.vcc, M1.DC_OUT+, Part1.5V, J3.vcc
  GND: BT1.GND, J1.gnd, M1.DC_OUT-, Part1.GND, J3.gnd
  N1: BT1.TXD, Part1.D10_PWM/SS
  N2: BT1.RXD, Part1.D11_PWM/MOSI
  N3: J1.pulse, Part1.D5_PWM
  N4: M1.IN-L, J2.pin2
  N5: M1.IN-N, J2.pin1
  N6: Part1.D6_PWM, J3.pulse

custom parts:
  Bluetooth HC-06u: Bluetooth HC-06 - face up, pins down 16.5mm x 37.5mm PCB
  WX-DC12003: Ac to DC power supply 110/220V in 5v 700ma or 12 V 300ma out.
  220v plug: Generic 220V AC plug.
